// Logisim project EL.circ as structural Verilog
module main (
  input  in_1,
  input  in_2,
  input  in_3,
  input  in_4,
  input  in_5,
  input  in_6,
  input  in_7,
  input  in_8,
  input  in_9,
  input  in_10,
  input  in_11,
  input  in_12,
  input  in_13,
  input  in_14,
  input  in_15,
  input  in_16,
  input  in_17,
  input  per_km_fare,
  input  in_19,
  input  in_20,
  input  in_21,
  input  INITIAL_CHARGES,
  input  in_23,
  input  in_24,
  input  in_25,
  input  in_26,
  input  in_27,
  input  in_28,
  input  in_29,
  input  in_30,
  input  in_31
);

  wire bcd_7segment_1_a_2, bcd_7segment_1_b_2, bcd_7segment_1_c_2, bcd_7segment_1_d_2, bcd_7segment_1_e,
       bcd_7segment_1_f, bcd_7segment_1_g, bcd_7segment_2_a_2, bcd_7segment_2_b_2, bcd_7segment_2_c_2,
       bcd_7segment_2_d_2, bcd_7segment_2_e, bcd_7segment_2_f, bcd_7segment_2_g, bcd_7segment_3_a_2,
       bcd_7segment_3_b_2, bcd_7segment_3_c_2, bcd_7segment_3_d_2, bcd_7segment_3_e, bcd_7segment_3_f,
       bcd_7segment_3_g, bcd_7segment_4_a_2, bcd_7segment_4_b_2, bcd_7segment_4_c_2, bcd_7segment_4_d_2,
       bcd_7segment_4_e, bcd_7segment_4_f, bcd_7segment_4_g, binary_division_1_q0, binary_division_1_q1,
       binary_division_1_q2, binary_division_1_q3, binary_division_1_q4, binary_division_1_q5,
       binary_division_1_q6, binary_division_1_q7, clock_1_out, n2_1_12bit_multiplexers_1_s0,
       n2_1_12bit_multiplexers_1_s1, n2_1_12bit_multiplexers_1_s2, n2_1_12bit_multiplexers_1_s3,
       n2_1_12bit_multiplexers_1_s4, n2_1_12bit_multiplexers_1_s5, n2_1_12bit_multiplexers_1_s6,
       n2_1_12bit_multiplexers_1_s7, n2_1_12bit_multiplexers_1_s8, n2_1_12bit_multiplexers_1_s9,
       n2_1_12bit_multiplexers_1_s10, n2_1_12bit_multiplexers_1_s11, n8_bit_adder_1_cout, n8_bit_adder_1_s0,
       n8_bit_adder_1_s1, n8_bit_adder_1_s2, n8_bit_adder_1_s3, n8_bit_adder_1_s4, n8_bit_adder_1_s5,
       n8_bit_adder_1_s6, n8_bit_adder_1_s7, n8x3_multiplier_1_s0, n8x3_multiplier_1_s1,
       n8x3_multiplier_1_s2, n8x3_multiplier_1_s3, n8x3_multiplier_1_s4, n8x3_multiplier_1_s5,
       n8x3_multiplier_1_s6, n8x3_multiplier_1_s7, n8x3_multiplier_1_s8, n8x3_multiplier_1_s9,
       n10_x_3_binary_multiplier_1_s0, n10_x_3_binary_multiplier_1_s1, n10_x_3_binary_multiplier_1_s2,
       n10_x_3_binary_multiplier_1_s3, n10_x_3_binary_multiplier_1_s4, n10_x_3_binary_multiplier_1_s5,
       n10_x_3_binary_multiplier_1_s6, n10_x_3_binary_multiplier_1_s7, n10_x_3_binary_multiplier_1_s8,
       n10_x_3_binary_multiplier_1_s9, n10_x_3_binary_multiplier_1_s10, n10_x_3_binary_multiplier_1_s11,
       n12_bit_adder_1_s0, n12_bit_adder_1_s1, n12_bit_adder_1_s1_2, n12_bit_adder_1_s2,
       n12_bit_adder_1_s2_2, n12_bit_adder_1_s3, n12_bit_adder_1_s3_2, n12_bit_adder_1_s4,
       n12_bit_adder_1_s5, n12_bit_adder_1_s6, n12_bit_adder_1_s7, n12_bit_adder_1_s8, n12_bit_adder_2_cout,
       n12_bit_adder_2_s0, n12_bit_adder_2_s1, n12_bit_adder_2_s1_2, n12_bit_adder_2_s2,
       n12_bit_adder_2_s2_2, n12_bit_adder_2_s3, n12_bit_adder_2_s3_2, n12_bit_adder_2_s4,
       n12_bit_adder_2_s5, n12_bit_adder_2_s6, n12_bit_adder_2_s7, n12_bit_adder_2_s8;

  BCD_7segment bcd_7segment_1 (
    .D(1'b0), .C(1'b0), .B(1'b0), .A(n12_bit_adder_2_cout), .a_2(bcd_7segment_1_a_2),
    .b_2(bcd_7segment_1_b_2), .c_2(bcd_7segment_1_c_2), .d_2(bcd_7segment_1_d_2), .e(bcd_7segment_1_e),
    .f(bcd_7segment_1_f), .g(bcd_7segment_1_g));
  _7_Segment_Display u_7_segment_display_1 (
    .g(bcd_7segment_1_g), .f(bcd_7segment_1_f), .a(bcd_7segment_1_a_2), .b(bcd_7segment_1_b_2),
    .e(bcd_7segment_1_e), .d(bcd_7segment_1_d_2), .c(bcd_7segment_1_c_2));  // open: dp
  BCD_7segment bcd_7segment_2 (
    .D(n12_bit_adder_2_s3_2), .C(n12_bit_adder_2_s2_2), .B(n12_bit_adder_2_s1_2), .A(n12_bit_adder_2_s8),
    .a_2(bcd_7segment_2_a_2), .b_2(bcd_7segment_2_b_2), .c_2(bcd_7segment_2_c_2), .d_2(bcd_7segment_2_d_2),
    .e(bcd_7segment_2_e), .f(bcd_7segment_2_f), .g(bcd_7segment_2_g));
  _7_Segment_Display u_7_segment_display_2 (
    .g(bcd_7segment_2_g), .f(bcd_7segment_2_f), .a(bcd_7segment_2_a_2), .b(bcd_7segment_2_b_2),
    .e(bcd_7segment_2_e), .d(bcd_7segment_2_d_2), .c(bcd_7segment_2_c_2));  // open: dp
  _2_1__12bit__multiplexers u_2_1_12bit_multiplexers_1 (
    .condition(n8_bit_adder_1_cout), .A11(1'b0), .A10(1'b0), .A9(1'b0), .A8(1'b0), .A7(in_20), .A6(in_21),
    .A5(INITIAL_CHARGES), .A4(in_23), .A3(in_24), .A2(in_25), .A1(in_26), .A0(in_27),
    .B11(n12_bit_adder_1_s3_2), .B10(n12_bit_adder_1_s2_2), .B9(n12_bit_adder_1_s1_2),
    .B8(n12_bit_adder_1_s8), .B7(n12_bit_adder_1_s7), .B6(n12_bit_adder_1_s6), .B5(n12_bit_adder_1_s5),
    .B4(n12_bit_adder_1_s4), .B3(n12_bit_adder_1_s3), .B2(n12_bit_adder_1_s2), .B1(n12_bit_adder_1_s1),
    .B0(n12_bit_adder_1_s0), .S11(n2_1_12bit_multiplexers_1_s11), .S10(n2_1_12bit_multiplexers_1_s10),
    .S9(n2_1_12bit_multiplexers_1_s9), .S8(n2_1_12bit_multiplexers_1_s8), .S7(n2_1_12bit_multiplexers_1_s7),
    .S6(n2_1_12bit_multiplexers_1_s6), .S5(n2_1_12bit_multiplexers_1_s5), .S4(n2_1_12bit_multiplexers_1_s4),
    .S3(n2_1_12bit_multiplexers_1_s3), .S2(n2_1_12bit_multiplexers_1_s2), .S1(n2_1_12bit_multiplexers_1_s1),
    .S0(n2_1_12bit_multiplexers_1_s0));
  _10_x_3_binary_multiplier u_10_x_3_binary_multiplier_1 (
    .A9(1'b0), .A8(1'b0), .A7(n8_bit_adder_1_s7), .A6(n8_bit_adder_1_s6), .A5(n8_bit_adder_1_s5),
    .A4(n8_bit_adder_1_s4), .A3(n8_bit_adder_1_s3), .A2(n8_bit_adder_1_s2), .A1(n8_bit_adder_1_s1),
    .A0(n8_bit_adder_1_s0), .B2(in_17), .B1(per_km_fare), .B0(in_19), .S11(n10_x_3_binary_multiplier_1_s11),
    .S10(n10_x_3_binary_multiplier_1_s10), .S9(n10_x_3_binary_multiplier_1_s9),
    .S8(n10_x_3_binary_multiplier_1_s8), .S7(n10_x_3_binary_multiplier_1_s7),
    .S6(n10_x_3_binary_multiplier_1_s6), .S5(n10_x_3_binary_multiplier_1_s5),
    .S4(n10_x_3_binary_multiplier_1_s4), .S3(n10_x_3_binary_multiplier_1_s3),
    .S2(n10_x_3_binary_multiplier_1_s2), .S1(n10_x_3_binary_multiplier_1_s1),
    .S0(n10_x_3_binary_multiplier_1_s0));
  BCD_7segment bcd_7segment_3 (
    .D(n12_bit_adder_2_s7), .C(n12_bit_adder_2_s6), .B(n12_bit_adder_2_s5), .A(n12_bit_adder_2_s4),
    .a_2(bcd_7segment_3_a_2), .b_2(bcd_7segment_3_b_2), .c_2(bcd_7segment_3_c_2), .d_2(bcd_7segment_3_d_2),
    .e(bcd_7segment_3_e), .f(bcd_7segment_3_f), .g(bcd_7segment_3_g));
  _7_Segment_Display u_7_segment_display_3 (
    .g(bcd_7segment_3_g), .f(bcd_7segment_3_f), .a(bcd_7segment_3_a_2), .b(bcd_7segment_3_b_2),
    .e(bcd_7segment_3_e), .d(bcd_7segment_3_d_2), .c(bcd_7segment_3_c_2));  // open: dp
  binary_division binary_division_1 (
    .CLK(clock_1_out), .\initial (in_28), .A11(n2_1_12bit_multiplexers_1_s11),
    .A10(n2_1_12bit_multiplexers_1_s10), .A9(n2_1_12bit_multiplexers_1_s9),
    .A8_2(n2_1_12bit_multiplexers_1_s8), .A7(n2_1_12bit_multiplexers_1_s7),
    .A6(n2_1_12bit_multiplexers_1_s6), .A5(n2_1_12bit_multiplexers_1_s5), .A4(n2_1_12bit_multiplexers_1_s4),
    .A8(n2_1_12bit_multiplexers_1_s3), .A2(n2_1_12bit_multiplexers_1_s2), .A1(n2_1_12bit_multiplexers_1_s1),
    .A0(n2_1_12bit_multiplexers_1_s0), .q7(binary_division_1_q7), .q6(binary_division_1_q6),
    .q5(binary_division_1_q5), .q4(binary_division_1_q4), .q3(binary_division_1_q3),
    .q2(binary_division_1_q2), .q1(binary_division_1_q1), .q0(binary_division_1_q0));  // open: q8
  Clock clock_1 (.out(clock_1_out));
  _8_BIT_ADDER u_8_bit_adder_1 (
    .Cout(n8_bit_adder_1_cout), .A7(in_1), .A6(in_2), .A5(in_3), .A4(in_4), .A3(in_5), .A2(in_6), .A1(in_7),
    .A0(in_8), .B7(in_9), .B6(in_10), .B5(in_11), .B4(in_12), .B3(in_13), .B2(in_14), .B1(in_15), .B0(in_16),
    .S7(n8_bit_adder_1_s7), .S6(n8_bit_adder_1_s6), .S5(n8_bit_adder_1_s5), .S4(n8_bit_adder_1_s4),
    .S3(n8_bit_adder_1_s3), .S2(n8_bit_adder_1_s2), .S1(n8_bit_adder_1_s1), .S0(n8_bit_adder_1_s0), .Cin(1'b1));
  _12_bit_adder u_12_bit_adder_1 (
    .A11(1'b0), .A10(1'b0), .A9(1'b0), .A8(1'b0), .A7(in_20), .A6(in_21), .A5(INITIAL_CHARGES), .A4(in_23),
    .A3(in_24), .A2(in_25), .A1(in_26), .A0(in_27), .B11(n10_x_3_binary_multiplier_1_s11),
    .B10(n10_x_3_binary_multiplier_1_s10), .B9(n10_x_3_binary_multiplier_1_s9),
    .B8(n10_x_3_binary_multiplier_1_s8), .B7(n10_x_3_binary_multiplier_1_s7),
    .B6(n10_x_3_binary_multiplier_1_s6), .B5(n10_x_3_binary_multiplier_1_s5),
    .B4(n10_x_3_binary_multiplier_1_s4), .B3(n10_x_3_binary_multiplier_1_s3),
    .B2(n10_x_3_binary_multiplier_1_s2), .B1(n10_x_3_binary_multiplier_1_s1),
    .B0(n10_x_3_binary_multiplier_1_s0), .S3_2(n12_bit_adder_1_s3_2), .S2_2(n12_bit_adder_1_s2_2),
    .S1_2(n12_bit_adder_1_s1_2), .S8(n12_bit_adder_1_s8), .S7(n12_bit_adder_1_s7), .S6(n12_bit_adder_1_s6),
    .S5(n12_bit_adder_1_s5), .S4(n12_bit_adder_1_s4), .S3(n12_bit_adder_1_s3), .S2(n12_bit_adder_1_s2),
    .S1(n12_bit_adder_1_s1), .S0(n12_bit_adder_1_s0), .Cin(1'b0));  // open: Cout
  _8X3_multiplier u_8x3_multiplier_1 (
    .A7(binary_division_1_q7), .A6(binary_division_1_q6), .A5(binary_division_1_q5),
    .A4(binary_division_1_q4), .A3(binary_division_1_q3), .A2(binary_division_1_q2),
    .A1(binary_division_1_q1), .A0(binary_division_1_q0), .B2(in_29), .B1(in_30), .B0(in_31),
    .S9(n8x3_multiplier_1_s9), .S8(n8x3_multiplier_1_s8), .S7(n8x3_multiplier_1_s7),
    .S6(n8x3_multiplier_1_s6), .S5(n8x3_multiplier_1_s5), .S4(n8x3_multiplier_1_s4),
    .S3(n8x3_multiplier_1_s3), .S2(n8x3_multiplier_1_s2), .S1(n8x3_multiplier_1_s1), .S0(n8x3_multiplier_1_s0));
  _12_bit_adder u_12_bit_adder_2 (
    .Cout(n12_bit_adder_2_cout), .A11(n2_1_12bit_multiplexers_1_s11), .A10(n2_1_12bit_multiplexers_1_s10),
    .A9(n2_1_12bit_multiplexers_1_s9), .A8(n2_1_12bit_multiplexers_1_s8), .A7(n2_1_12bit_multiplexers_1_s7),
    .A6(n2_1_12bit_multiplexers_1_s6), .A5(n2_1_12bit_multiplexers_1_s5), .A4(n2_1_12bit_multiplexers_1_s4),
    .A3(n2_1_12bit_multiplexers_1_s3), .A2(n2_1_12bit_multiplexers_1_s2), .A1(n2_1_12bit_multiplexers_1_s1),
    .A0(n2_1_12bit_multiplexers_1_s0), .B11(1'b0), .B10(1'b0), .B9(n8x3_multiplier_1_s9),
    .B8(n8x3_multiplier_1_s8), .B7(n8x3_multiplier_1_s7), .B6(n8x3_multiplier_1_s6),
    .B5(n8x3_multiplier_1_s5), .B4(n8x3_multiplier_1_s4), .B3(n8x3_multiplier_1_s3),
    .B2(n8x3_multiplier_1_s2), .B1(n8x3_multiplier_1_s1), .B0(n8x3_multiplier_1_s0),
    .S3_2(n12_bit_adder_2_s3_2), .S2_2(n12_bit_adder_2_s2_2), .S1_2(n12_bit_adder_2_s1_2),
    .S8(n12_bit_adder_2_s8), .S7(n12_bit_adder_2_s7), .S6(n12_bit_adder_2_s6), .S5(n12_bit_adder_2_s5),
    .S4(n12_bit_adder_2_s4), .S3(n12_bit_adder_2_s3), .S2(n12_bit_adder_2_s2), .S1(n12_bit_adder_2_s1),
    .S0(n12_bit_adder_2_s0), .Cin(1'b0));
  _7_Segment_Display u_7_segment_display_4 (
    .g(bcd_7segment_4_g), .f(bcd_7segment_4_f), .a(bcd_7segment_4_a_2), .b(bcd_7segment_4_b_2),
    .e(bcd_7segment_4_e), .d(bcd_7segment_4_d_2), .c(bcd_7segment_4_c_2));  // open: dp
  BCD_7segment bcd_7segment_4 (
    .D(n12_bit_adder_2_s3), .C(n12_bit_adder_2_s2), .B(n12_bit_adder_2_s1), .A(n12_bit_adder_2_s0),
    .a_2(bcd_7segment_4_a_2), .b_2(bcd_7segment_4_b_2), .c_2(bcd_7segment_4_c_2), .d_2(bcd_7segment_4_d_2),
    .e(bcd_7segment_4_e), .f(bcd_7segment_4_f), .g(bcd_7segment_4_g));

  // Notes on the sheet:
  //   distance of travel
  //   mandatory distance
  //   TOTAL TAXI FARE = ((DISTANCE OF TRAVEL---MANDATORY DISTANCE) X PER_KM_FARE + INITIAL CHARGES)
endmodule

module BCD_7segment (
  input  D,
  input  C,
  input  B,
  input  A,
  output a_2,
  output b_2,
  output c_2,
  output d_2,
  output e,
  output f,
  output g
);

  wire and_1_out, and_2_out, and_3_out, and_4_out, and_5_out, and_6_out, and_7_out, and_8_out, and_9_out,
       and_10_out, and_11_out, and_12_out, and_13_out, and_14_out, and_15_out, and_16_out, and_17_out,
       not_1_out, not_2_out, not_3_out, not_4_out, not_5_out, not_6_out, not_7_out, not_8_out, not_9_out,
       not_10_out, not_11_out, not_12_out, not_13_out, not_14_out, not_15_out, not_16_out, not_17_out,
       not_18_out, not_19_out, not_20_out, not_21_out, or_1_out, or_2_out, or_4_out, or_5_out, or_8_out,
       or_9_out, or_10_out, or_12_out, or_14_out, or_15_out, or_17_out;

  not not_1 (not_1_out, C);
  not not_2 (not_2_out, A);
  not not_3 (not_3_out, B);
  not not_4 (not_4_out, A);
  not not_5 (not_5_out, B);
  not not_6 (not_6_out, C);
  not not_7 (not_7_out, A);
  not not_8 (not_8_out, C);
  not not_9 (not_9_out, B);
  not not_10 (not_10_out, C);
  not not_11 (not_11_out, A);
  not not_12 (not_12_out, A);
  not not_13 (not_13_out, B);
  not not_14 (not_14_out, A);
  not not_15 (not_15_out, B);
  not not_16 (not_16_out, A);
  not not_17 (not_17_out, C);
  not not_18 (not_18_out, B);
  not not_19 (not_19_out, A);
  and and_1 (and_1_out, not_1_out, not_2_out);
  and and_2 (and_2_out, C, A);
  not not_20 (not_20_out, C);
  and and_3 (and_3_out, not_3_out, not_4_out);
  or or_1 (or_1_out, not_5_out, A);
  and and_4 (and_4_out, not_6_out, not_7_out);
  and and_5 (and_5_out, not_8_out, B);
  not not_21 (not_21_out, A);
  and and_6 (and_6_out, C, not_9_out);
  and and_7 (and_7_out, not_10_out, not_11_out);
  and and_8 (and_8_out, B, not_12_out);
  and and_9 (and_9_out, not_13_out, not_14_out);
  and and_10 (and_10_out, C, not_15_out);
  and and_11 (and_11_out, C, not_16_out);
  and and_12 (and_12_out, not_17_out, B);
  and and_13 (and_13_out, C, not_18_out);
  and and_14 (and_14_out, C, not_19_out);
  or or_2 (or_2_out, and_1_out, B);
  or or_3 (a_2, or_2_out, or_4_out);
  or or_4 (or_4_out, and_2_out, D);
  or or_5 (or_5_out, not_20_out, and_3_out);
  or or_6 (b_2, or_5_out, and_15_out);
  and and_15 (and_15_out, B, A);
  or or_7 (c_2, or_1_out, C);
  or or_8 (or_8_out, and_4_out, and_5_out);
  or or_9 (or_9_out, or_8_out, and_16_out);
  and and_16 (and_16_out, B, not_21_out);
  and and_17 (and_17_out, and_6_out, A);
  or or_10 (or_10_out, and_17_out, D);
  or or_11 (e, and_7_out, and_8_out);
  or or_12 (or_12_out, and_9_out, and_10_out);
  or or_13 (f, or_12_out, or_14_out);
  or or_14 (or_14_out, and_11_out, D);
  or or_15 (or_15_out, and_12_out, and_13_out);
  or or_16 (g, or_15_out, or_17_out);
  or or_17 (or_17_out, and_14_out, D);
  or or_18 (d_2, or_9_out, or_10_out);
endmodule

module _12_bit_3_bit_multiplier (
  input  A9,
  input  A8,
  input  A7,
  input  A6,
  input  A5,
  input  A4,
  input  A3,
  input  A2,
  input  A1,
  input  A0,
  input  B2,
  input  B1,
  input  B0,
  output S11,
  output S10,
  output S9,
  output S8,
  output S7,
  output S6,
  output S5,
  output S4,
  output S3,
  output S1,
  output S0,
  output S2
);

  wire and_2_out, and_3_out, and_4_out, and_5_out, and_6_out, and_7_out, and_8_out, and_9_out, and_10_out,
       and_11_out, and_12_out, and_13_out, and_14_out, and_15_out, and_16_out, and_17_out, and_18_out,
       and_19_out, and_20_out, and_21_out, and_22_out, and_23_out, and_24_out, and_25_out, and_26_out,
       and_27_out, and_28_out, and_29_out, and_30_out, and_31_out, and_32_out, and_33_out, and_34_out,
       and_35_out, and_36_out, and_37_out, and_38_out, and_39_out;

  and and_1 (S0, B0, A0);
  and and_2 (and_2_out, A1, B0);
  and and_3 (and_3_out, A0, B1);
  and and_4 (and_4_out, A2, B0);
  and and_5 (and_5_out, A1, B1);
  and and_6 (and_6_out, A0, B2);
  and and_7 (and_7_out, A3, B0);
  and and_8 (and_8_out, A2, B1);
  and and_9 (and_9_out, A1, B2);
  and and_10 (and_10_out, A4, B0);
  and and_11 (and_11_out, A3, B1);
  and and_12 (and_12_out, A2, B2);
  and and_13 (and_13_out, A5, B0);
  and and_14 (and_14_out, A4, B1);
  and and_15 (and_15_out, A3, B2);
  and and_16 (and_16_out, A6, B0);
  and and_17 (and_17_out, A5, B1);
  and and_18 (and_18_out, A4, B2);
  and and_19 (and_19_out, A7, B0);
  and and_20 (and_20_out, A6, B1);
  and and_21 (and_21_out, A5, B2);
  and and_22 (and_22_out, A8, B0);
  and and_23 (and_23_out, A7, B1);
  and and_24 (and_24_out, A6, B2);
  and and_25 (and_25_out, A9, B0);
  and and_26 (and_26_out, A8, B1);
  and and_27 (and_27_out, A7, B2);
  and and_28 (and_28_out, A9, B1);
  and and_29 (and_29_out, A8, B2);
  xor xor_1 (S1, and_2_out, and_3_out);
  and and_30 (and_30_out, and_2_out, and_3_out);
  ExactlyOne xor_2 (.out(S2), .in0(and_30_out), .in1(and_4_out), .in2(and_5_out), .in3(and_6_out));
  and and_31 (and_31_out, and_4_out, and_5_out, and_6_out);
  ExactlyOne xor_3 (.out(S3), .in0(and_31_out), .in1(and_7_out), .in2(and_8_out), .in3(and_9_out));
  and and_32 (and_32_out, and_7_out, and_8_out, and_9_out);
  ExactlyOne xor_4 (.out(S4), .in0(and_32_out), .in1(and_10_out), .in2(and_11_out), .in3(and_12_out));
  and and_33 (and_33_out, and_10_out, and_11_out, and_12_out);
  ExactlyOne xor_5 (.out(S5), .in0(and_33_out), .in1(and_13_out), .in2(and_14_out), .in3(and_15_out));
  and and_34 (and_34_out, and_13_out, and_14_out, and_15_out);
  ExactlyOne xor_6 (.out(S6), .in0(and_34_out), .in1(and_16_out), .in2(and_17_out), .in3(and_18_out));
  and and_35 (and_35_out, and_16_out, and_17_out, and_18_out);
  and and_36 (and_36_out, and_19_out, and_20_out, and_21_out);
  and and_37 (and_37_out, and_22_out, and_23_out, and_24_out);
  ExactlyOne xor_7 (.out(S7), .in0(and_35_out), .in1(and_19_out), .in2(and_20_out), .in3(and_21_out));
  ExactlyOne xor_8 (.out(S8), .in0(and_36_out), .in1(and_22_out), .in2(and_23_out), .in3(and_24_out));
  ExactlyOne xor_9 (.out(S9), .in0(and_37_out), .in1(and_25_out), .in2(and_26_out), .in3(and_27_out));
  and and_38 (and_38_out, and_25_out, and_26_out, and_27_out);
  ExactlyOne xor_10 (.out(S10), .in0(and_38_out), .in1(and_28_out), .in2(and_29_out));
  and and_39 (and_39_out, and_28_out, and_29_out);
  and and_40 (S11, and_39_out, A9, B2);

  // Notes on the sheet:
  //   P0
  //   P1
  //   p2
  //   p3
  //   p4
  //   p5
  //   p6
  //   p7
  //   p8
  //   p11
  //   p9
  //   p10
endmodule

module quotient_register (
  input  serial_input,
  output q0,
  output q1,
  output q2,
  output q3,
  output q4,
  output q5,
  output q6,
  output q7,
  output q8,
  output q9
);

  wire and_1_out, and_2_out, and_3_out, and_4_out, and_5_out, and_6_out, and_7_out, and_8_out, and_9_out,
       and_10_out, and_11_out, and_12_out, and_13_out, and_14_out, and_15_out, and_16_out, and_17_out,
       and_18_out, not_1_out, or_1_out, or_2_out, or_3_out, or_4_out, or_5_out, or_6_out, or_7_out, or_8_out,
       or_9_out, quotient_clk_out;

  not not_1 (not_1_out, 1'b1);
  and and_1 (and_1_out, q0, 1'b1);
  D_Flip_Flop d_ff_1 (
    .clk(quotient_clk_out), .D(serial_input), .Q(q0), .preset(1'b0), .en(1'b1), .reset(1'b0));  // open: Qn
  Clock quotient_clk (.out(quotient_clk_out));
  and and_2 (and_2_out, not_1_out, 1'b0);
  or or_1 (or_1_out, and_1_out, and_2_out);
  and and_3 (and_3_out, q1, 1'b1);
  or or_2 (or_2_out, and_3_out, and_5_out);
  // D_Flip_Flop d_flip_flop_1: pin names not known; wires that end beside it: or_1_out, quotient_clk_out, q1
  and and_4 (and_4_out, q2, 1'b1);
  and and_5 (and_5_out, not_1_out, 1'b0);
  // D_Flip_Flop d_flip_flop_2: pin names not known; wires that end beside it: or_2_out, quotient_clk_out, q2
  and and_6 (and_6_out, not_1_out, 1'b0);
  or or_3 (or_3_out, and_4_out, and_6_out);
  // D_Flip_Flop d_flip_flop_3: pin names not known; wires that end beside it: or_3_out, quotient_clk_out, q3
  and and_7 (and_7_out, not_1_out, 1'b0);
  and and_8 (and_8_out, q3, 1'b1);
  or or_4 (or_4_out, and_8_out, and_7_out);
  and and_9 (and_9_out, q4, 1'b1);
  or or_5 (or_5_out, and_9_out, and_10_out);
  // D_Flip_Flop d_flip_flop_4: pin names not known; wires that end beside it: or_4_out, quotient_clk_out, q4
  and and_10 (and_10_out, not_1_out, 1'b0);
  // D_Flip_Flop d_flip_flop_5: pin names not known; wires that end beside it: or_5_out, quotient_clk_out, q5
  and and_11 (and_11_out, not_1_out, 1'b0);
  and and_12 (and_12_out, q5, 1'b1);
  or or_6 (or_6_out, and_12_out, and_11_out);
  and and_13 (and_13_out, q6, 1'b1);
  // D_Flip_Flop d_flip_flop_6: pin names not known; wires that end beside it: or_6_out, quotient_clk_out
  and and_14 (and_14_out, not_1_out, 1'b0);
  or or_7 (or_7_out, and_13_out, and_14_out);
  and and_15 (and_15_out, q7, 1'b1);
  or or_8 (or_8_out, and_15_out, and_16_out);
  // D_Flip_Flop d_flip_flop_7: pin names not known; wires that end beside it: or_7_out, quotient_clk_out, q7
  and and_16 (and_16_out, not_1_out, 1'b0);
  and and_17 (and_17_out, q8, 1'b1);
  // D_Flip_Flop d_flip_flop_8: pin names not known; wires that end beside it: or_8_out, quotient_clk_out, q8, q8
  and and_18 (and_18_out, not_1_out, 1'b0);
  or or_9 (or_9_out, and_17_out, and_18_out);
  // D_Flip_Flop d_flip_flop_9: pin names not known; wires that end beside it: or_9_out, quotient_clk_out, q9
endmodule

module _12_bit_adder (
  input  B11,
  input  B10,
  input  B9,
  input  B8,
  input  B7,
  input  B6,
  input  B5,
  input  B4,
  input  B3,
  input  B2,
  input  B1,
  input  B0,
  input  Cin,
  input  A5,
  input  A4,
  input  A0,
  input  A8,
  input  A2,
  input  A1,
  input  A10,
  input  A9,
  input  A6,
  input  A3,
  input  A11,
  input  A7,
  output S0,
  output S8,
  output S1,
  output S1_2,
  output S2,
  output S2_2,
  output S3,
  output Cout,
  output S3_2,
  output S5,
  output S6,
  output S7,
  output S4
);

  wire ic_74283_1_p1, ic_74283_1_p11, ic_74283_1_p13, ic_74283_2_p1, ic_74283_2_p11, ic_74283_2_p13,
       ic_74283_3_p11, ic_74283_3_p13, xor_1_out, xor_2_out, xor_5_out, xor_6_out, xor_9_out, xor_10_out;

  xor xor_1 (xor_1_out, Cin, B11);
  xor xor_2 (xor_2_out, Cin, B10);
  // IC_74283 ic_74283_1: pin names not known; wires that end beside it: ic_74283_1_p1, Cout, A11, A10, A9, A8, xor_1_out, S3_2, xor_2_out, S2_2, ic_74283_1_p11, S1_2, ic_74283_1_p13, S8
  xor xor_3 (ic_74283_1_p11, Cin, B9);
  xor xor_4 (ic_74283_1_p13, Cin, B8);
  xor xor_5 (xor_5_out, Cin, B7);
  xor xor_6 (xor_6_out, Cin, B6);
  // IC_74283 ic_74283_2: pin names not known; wires that end beside it: ic_74283_2_p1, ic_74283_1_p1, A7, A6, A5, A4, xor_5_out, S7, xor_6_out, S6, ic_74283_2_p11, S5, ic_74283_2_p13, S4
  xor xor_7 (ic_74283_2_p11, Cin, B5);
  xor xor_8 (ic_74283_2_p13, Cin, B4);
  xor xor_9 (xor_9_out, Cin, B3);
  xor xor_10 (xor_10_out, Cin, B2);
  // IC_74283 ic_74283_3: pin names not known; wires that end beside it: Cin, ic_74283_2_p1, A3, A2, A1, A0, xor_9_out, S3, xor_10_out, S2, ic_74283_3_p11, S1, ic_74283_3_p13, S0
  xor xor_11 (ic_74283_3_p11, Cin, B1);
  xor xor_12 (ic_74283_3_p13, Cin, B0);

  // Notes on the sheet:
  //   subtraction
endmodule

module binary_division (
  input  A0,
  input  A1,
  input  A8,
  input  A2,
  input  A4,
  input  A5,
  input  A6,
  input  A7,
  input  A8_2,
  input  A9,
  input  A10,
  input  A11,
  input  CLK,
  input  \initial ,
  output q0,
  output q2,
  output q1,
  output q3,
  output q4,
  output q5,
  output q6,
  output q7,
  output q8
);

  wire and_1_out, and_2_out, and_3_out, and_4_out, and_5_out, and_6_out, and_7_out, and_8_out, and_9_out,
       and_10_out, and_11_out, and_12_out, and_13_out, and_14_out, and_15_out, and_16_out, and_17_out,
       and_18_out, and_19_out, and_20_out, and_21_out, and_22_out, and_23_out, and_24_out, and_25_out,
       and_26_out, and_27_out, and_28_out, and_29_out, and_30_out, and_31_out, and_32_out, and_33_out,
       and_34_out, and_35_out, and_36_out, and_37_out, and_38_out, and_39_out, and_40_out, and_41_out,
       and_42_out, and_43_out, and_44_out, d_flip_flop_1_p2, d_flip_flop_1_p4, d_flip_flop_2_p4,
       d_flip_flop_3_p3, d_flip_flop_4_p3, d_flip_flop_5_p3, d_flip_flop_5_p4, d_flip_flop_5_p5,
       d_flip_flop_6_p3, d_flip_flop_6_p4, d_flip_flop_10_p2, d_flip_flop_12_p1, d_flip_flop_12_p4,
       d_flip_flop_16_p3, d_flip_flop_17_p4, d_flip_flop_19_p4, d_flip_flop_20_p4, d_flip_flop_30_p3,
       ic_7485_1_p1, ic_7485_1_p2, ic_7485_1_p4, ic_7485_1_p5, ic_7485_1_p6, ic_7485_1_p7, ic_7485_1_p16,
       ic_74112_1_p5, ic_74112_1_p8, ic_74112_1_p12, ic_74112_2_p5, ic_74112_2_p12, ic_74283_1_p1,
       ic_74283_1_p2, ic_74283_1_p3, ic_74283_1_p4, ic_74283_1_p5, ic_74283_1_p6, ic_74283_1_p7,
       ic_74283_1_p16, ic_74283_2_p8, ic_74283_2_p10, ic_74283_2_p11, ic_74283_2_p12, ic_74283_2_p13,
       ic_74283_2_p14, multiplexer_1_out, multiplexer_2_out, multiplexer_3_out, multiplexer_4_out,
       multiplexer_5_out, multiplexer_6_out, multiplexer_7_out, multiplexer_8_out, multiplexer_9_out,
       multiplexer_10_out, nand_1_out, not_2_out, not_3_out, or_1_out, or_2_out, or_3_out, or_4_out,
       or_5_out, or_6_out, or_7_out, or_8_out, or_9_out, or_10_out, or_11_out, or_12_out, or_13_out,
       or_14_out, or_15_out, or_16_out, or_17_out, or_18_out, or_19_out, or_20_out, or_21_out, or_22_out,
       or_23_out, or_24_out, or_25_out, or_26_out, xor_1_out, xor_2_out;

  Multiplexer multiplexer_1 (.in0(CLK), .in1(1'b0), .out(multiplexer_1_out), .sel(not_3_out));  // open: en
  // D_Flip_Flop d_flip_flop_1: pin names not known; wires that end beside it: 1'b0, d_flip_flop_1_p2, \initial , d_flip_flop_1_p4
  not not_1 (d_flip_flop_1_p2, multiplexer_1_out);
  // D_Flip_Flop d_flip_flop_2: pin names not known; wires that end beside it: d_flip_flop_1_p4, d_flip_flop_1_p2, \initial , d_flip_flop_2_p4
  or or_1 (or_1_out, d_flip_flop_1_p4, or_26_out, and_8_out);
  or or_2 (or_2_out, d_flip_flop_2_p4, d_flip_flop_12_p1);
  and and_1 (and_1_out, d_flip_flop_3_p3, d_flip_flop_20_p4);
  or or_3 (or_3_out, and_1_out, and_3_out);
  // D_Flip_Flop d_flip_flop_3: pin names not known; wires that end beside it: A0, or_2_out, d_flip_flop_3_p3
  or or_4 (or_4_out, ic_7485_1_p5, ic_7485_1_p7);
  // IC_74283 ic_74283_1: pin names not known; wires that end beside it: ic_74283_1_p1, ic_74283_1_p2, ic_74283_1_p3, ic_74283_1_p4, ic_74283_1_p5, ic_74283_1_p6, ic_74283_1_p7, 1'b0, 1'b0, 1'b0, ic_74283_1_p1, 1'b1, 1'b1, 1'b1, 1'b1, ic_74283_1_p16
  and and_2 (and_2_out, d_flip_flop_4_p3, d_flip_flop_20_p4);
  and and_3 (and_3_out, or_1_out, A1);
  // D_Flip_Flop d_flip_flop_4: pin names not known; wires that end beside it: or_3_out, or_2_out, d_flip_flop_4_p3
  // IC_7485 ic_7485_1: pin names not known; wires that end beside it: ic_7485_1_p1, ic_7485_1_p2, ic_7485_1_p1, ic_7485_1_p4, ic_7485_1_p5, ic_7485_1_p6, ic_7485_1_p7, 1'b0, 1'b0, 1'b0, ic_74283_1_p1, 1'b0, 1'b0, 1'b0, 1'b0, ic_7485_1_p16
  and and_4 (and_4_out, or_1_out, A2);
  or or_5 (or_5_out, and_2_out, and_4_out);
  and and_5 (and_5_out, d_flip_flop_5_p4, d_flip_flop_20_p4);
  or or_6 (or_6_out, and_5_out, and_6_out);
  // D_Flip_Flop d_flip_flop_5: pin names not known; wires that end beside it: or_5_out, or_2_out, d_flip_flop_5_p3, d_flip_flop_5_p4, d_flip_flop_5_p5
  and and_6 (and_6_out, or_1_out, A8);
  // D_Flip_Flop d_flip_flop_6: pin names not known; wires that end beside it: or_6_out, or_2_out, d_flip_flop_6_p3, d_flip_flop_6_p4
  // IC_7485 ic_7485_2: pin names not known; wires that end beside it: 1'b0, ic_7485_1_p2, 1'b1, ic_7485_1_p4, 1'b0, ic_7485_1_p6, ic_74283_1_p2, ic_74283_1_p3, ic_74283_1_p4, ic_74283_1_p5, 1'b1, 1'b0, d_flip_flop_6_p4, 1'b1, 1'b0, d_flip_flop_5_p4
  Multiplexer multiplexer_2 (.in0(1'b0), .in1(1'b0), .out(multiplexer_2_out), .sel(or_4_out));  // open: en
  Multiplexer multiplexer_3 (.in0(1'b0), .in1(1'b1), .out(multiplexer_3_out), .sel(or_4_out));  // open: en
  xor xor_1 (xor_1_out, or_4_out, multiplexer_3_out);
  xor xor_2 (xor_2_out, or_4_out, multiplexer_2_out);
  // IC_74283 ic_74283_2: pin names not known; wires that end beside it: or_4_out, ic_74283_1_p6, ic_74283_1_p2, ic_74283_1_p3, ic_74283_1_p4, ic_74283_1_p5, xor_1_out, ic_74283_2_p8, xor_2_out, ic_74283_2_p10, ic_74283_2_p11, ic_74283_2_p12, ic_74283_2_p13, ic_74283_2_p14
  and and_7 (and_7_out, d_flip_flop_6_p4, d_flip_flop_20_p4);
  or or_7 (or_7_out, and_7_out, and_9_out);
  and and_8 (and_8_out, or_4_out, d_flip_flop_16_p3);
  Multiplexer multiplexer_4 (.in0(1'b0), .in1(1'b1), .out(multiplexer_4_out), .sel(or_4_out));  // open: en
  xor xor_3 (ic_74283_2_p11, or_4_out, multiplexer_4_out);
  and and_9 (and_9_out, or_1_out, A4);
  and and_10 (and_10_out, d_flip_flop_6_p3, d_flip_flop_20_p4);
  // D_Flip_Flop d_flip_flop_7: pin names not known; wires that end beside it: d_flip_flop_4_p3, or_7_out, or_2_out, d_flip_flop_6_p3, d_flip_flop_3_p3
  Multiplexer multiplexer_5 (.in0(1'b0), .in1(1'b0), .out(multiplexer_5_out), .sel(or_4_out));  // open: en
  xor xor_4 (ic_74283_2_p13, or_4_out, multiplexer_5_out);
  and and_11 (and_11_out, or_1_out, A5);
  or or_8 (or_8_out, and_10_out, and_11_out);
  and and_12 (and_12_out, d_flip_flop_5_p5, d_flip_flop_20_p4);
  or or_9 (or_9_out, and_12_out, and_13_out);
  // D_Flip_Flop d_flip_flop_8: pin names not known; wires that end beside it: or_8_out, or_2_out, d_flip_flop_5_p5
  not not_2 (not_2_out, 1'b1);
  and and_13 (and_13_out, or_1_out, A6);
  // D_Flip_Flop d_flip_flop_9: pin names not known; wires that end beside it: or_9_out, or_2_out, d_flip_flop_5_p3
  and and_14 (and_14_out, not_2_out, 1'b0);
  and and_15 (and_15_out, q0, 1'b1);
  or or_10 (or_10_out, and_15_out, and_14_out);
  // D_Flip_Flop d_flip_flop_10: pin names not known; wires that end beside it: or_4_out, d_flip_flop_10_p2, q0
  and and_16 (and_16_out, d_flip_flop_5_p3, d_flip_flop_20_p4);
  and and_17 (and_17_out, q1, 1'b1);
  or or_11 (or_11_out, and_17_out, and_19_out);
  // D_Flip_Flop d_flip_flop_11: pin names not known; wires that end beside it: or_10_out, d_flip_flop_10_p2, q1
  // D_Flip_Flop d_flip_flop_12: pin names not known; wires that end beside it: d_flip_flop_12_p1, d_flip_flop_1_p2, d_flip_flop_2_p4, d_flip_flop_12_p4, d_flip_flop_12_p4, d_flip_flop_1_p2
  and and_18 (and_18_out, or_1_out, A7);
  or or_12 (or_12_out, and_16_out, and_18_out);
  and and_19 (and_19_out, not_2_out, 1'b0);
  // D_Flip_Flop d_flip_flop_13: pin names not known; wires that end beside it: or_11_out, d_flip_flop_10_p2, q2
  // D_Flip_Flop d_flip_flop_14: pin names not known; wires that end beside it: d_flip_flop_2_p4, d_flip_flop_10_p2, d_flip_flop_1_p2
  and and_20 (and_20_out, ic_7485_1_p16, d_flip_flop_20_p4);
  or or_13 (or_13_out, and_20_out, and_24_out);
  // D_Flip_Flop d_flip_flop_15: pin names not known; wires that end beside it: or_12_out, or_2_out, ic_7485_1_p16
  or or_14 (or_14_out, d_flip_flop_12_p1, and_31_out, d_flip_flop_2_p4);
  and and_21 (and_21_out, q2, 1'b1);
  and and_22 (and_22_out, not_2_out, 1'b0);
  or or_15 (or_15_out, and_21_out, and_22_out);
  // D_Flip_Flop d_flip_flop_16: pin names not known; wires that end beside it: d_flip_flop_10_p2, d_flip_flop_2_p4, d_flip_flop_16_p3
  Multiplexer multiplexer_6 (.in0(A8_2), .in1(ic_74283_2_p14), .out(multiplexer_6_out), .sel(or_26_out));  // open: en
  and and_23 (and_23_out, ic_74283_1_p5, d_flip_flop_20_p4);
  and and_24 (and_24_out, or_1_out, multiplexer_6_out);
  // D_Flip_Flop d_flip_flop_17: pin names not known; wires that end beside it: or_13_out, or_14_out, ic_74283_1_p5, d_flip_flop_17_p4, d_flip_flop_17_p4
  // D_Flip_Flop d_flip_flop_18: pin names not known; wires that end beside it: or_15_out, d_flip_flop_10_p2, q3
  // D_Flip_Flop d_flip_flop_19: pin names not known; wires that end beside it: d_flip_flop_16_p3, d_flip_flop_1_p2, d_flip_flop_2_p4, d_flip_flop_19_p4
  Multiplexer multiplexer_7 (.in0(A9), .in1(ic_74283_2_p12), .out(multiplexer_7_out), .sel(or_26_out));  // open: en
  and and_25 (and_25_out, or_1_out, multiplexer_7_out);
  or or_16 (or_16_out, and_23_out, and_25_out);
  and and_26 (and_26_out, q3, 1'b1);
  or or_17 (or_17_out, and_26_out, and_28_out);
  // D_Flip_Flop d_flip_flop_20: pin names not known; wires that end beside it: d_flip_flop_19_p4, d_flip_flop_1_p2, d_flip_flop_2_p4, d_flip_flop_20_p4, d_flip_flop_20_p4, d_flip_flop_1_p2
  // D_Flip_Flop d_flip_flop_21: pin names not known; wires that end beside it: or_16_out, or_14_out, ic_74283_1_p4
  and and_27 (and_27_out, q4, 1'b1);
  and and_28 (and_28_out, not_2_out, 1'b0);
  // D_Flip_Flop d_flip_flop_22: pin names not known; wires that end beside it: or_17_out, d_flip_flop_10_p2, q4
  // D_Flip_Flop d_flip_flop_23: pin names not known; wires that end beside it: d_flip_flop_2_p4, d_flip_flop_12_p1
  // IC_74112 ic_74112_1: pin names not known; wires that end beside it: 1'b1, d_flip_flop_16_p3, 1'b1, 1'b1, ic_74112_1_p5, 1'b1, 1'b1, ic_74112_1_p8, 1'b1, ic_74112_1_p8, ic_74112_1_p5, ic_74112_1_p12
  and and_29 (and_29_out, ic_74283_1_p4, d_flip_flop_20_p4);
  or or_18 (or_18_out, and_29_out, and_32_out);
  and and_30 (and_30_out, not_2_out, 1'b0);
  or or_19 (or_19_out, and_27_out, and_30_out);
  and and_31 (and_31_out, or_4_out, d_flip_flop_19_p4);
  not not_3 (not_3_out, nand_1_out);
  Multiplexer multiplexer_8 (.in0(A10), .in1(ic_74283_2_p10), .out(multiplexer_8_out), .sel(or_26_out));  // open: en
  and and_32 (and_32_out, or_1_out, multiplexer_8_out);
  and and_33 (and_33_out, ic_74283_1_p3, d_flip_flop_20_p4);
  // D_Flip_Flop d_flip_flop_24: pin names not known; wires that end beside it: or_18_out, or_14_out, ic_74283_1_p3
  and and_34 (and_34_out, q5, 1'b1);
  or or_20 (or_20_out, and_34_out, and_36_out);
  // D_Flip_Flop d_flip_flop_25: pin names not known; wires that end beside it: or_19_out, d_flip_flop_10_p2, q5
  // IC_74112 ic_74112_2: pin names not known; wires that end beside it: 1'b1, ic_74112_1_p12, 1'b1, 1'b1, ic_74112_2_p5, 1'b1, 1'b1, ic_74112_1_p8, 1'b1, ic_74112_1_p8, ic_74112_2_p5, ic_74112_2_p12, ic_74112_2_p12, ic_74112_2_p5, ic_74112_1_p12
  Multiplexer multiplexer_9 (.in0(A11), .in1(ic_74283_2_p8), .out(multiplexer_9_out), .sel(or_26_out));  // open: en
  and and_35 (and_35_out, or_1_out, multiplexer_9_out);
  or or_21 (or_21_out, and_33_out, and_35_out);
  and and_36 (and_36_out, not_2_out, 1'b0);
  // D_Flip_Flop d_flip_flop_26: pin names not known; wires that end beside it: or_20_out, d_flip_flop_10_p2
  nand nand_1 (nand_1_out, ic_74112_2_p12, ic_74112_1_p5);
  and and_37 (and_37_out, ic_74283_1_p2, d_flip_flop_20_p4);
  or or_22 (or_22_out, and_37_out, and_40_out);
  // D_Flip_Flop d_flip_flop_27: pin names not known; wires that end beside it: or_21_out, or_14_out, ic_74283_1_p2, or_14_out
  and and_38 (and_38_out, not_2_out, 1'b0);
  and and_39 (and_39_out, q6, 1'b1);
  or or_23 (or_23_out, and_39_out, and_38_out);
  Multiplexer multiplexer_10 (.in0(1'b0), .in1(ic_74283_1_p16), .out(multiplexer_10_out), .sel(or_26_out));  // open: en
  and and_40 (and_40_out, or_1_out, multiplexer_10_out);
  // IC_74175 ic_74175_1: pin names not known; wires that end beside it: or_22_out, ic_74283_1_p1, or_1_out, d_flip_flop_20_p4
  and and_41 (and_41_out, q7, 1'b1);
  // D_Flip_Flop d_flip_flop_28: pin names not known; wires that end beside it: or_23_out, d_flip_flop_10_p2, q7
  and and_42 (and_42_out, not_2_out, 1'b0);
  or or_24 (or_24_out, and_41_out, and_42_out);
  // D_Flip_Flop d_flip_flop_29: pin names not known; wires that end beside it: or_24_out, d_flip_flop_10_p2, q8
  and and_43 (and_43_out, not_2_out, 1'b0);
  and and_44 (and_44_out, q8, 1'b1);
  or or_25 (or_25_out, and_44_out, and_43_out);
  // D_Flip_Flop d_flip_flop_30: pin names not known; wires that end beside it: or_25_out, d_flip_flop_10_p2, d_flip_flop_30_p3, d_flip_flop_30_p3
  or or_26 (or_26_out, ic_74283_1_p7, d_flip_flop_19_p4);

  // Notes on the sheet:
  //   feed
  //   13  bit shift register
  //   1 for all
  //   feed and shift
  //   1
  //   1
  //   0-initial
  //   CLK
  //   MSB
endmodule

module _8_BIT_ADDER (
  input  B7,
  input  B6,
  input  B5,
  input  B4,
  input  B3,
  input  B2,
  input  B1,
  input  B0,
  input  Cin,
  input  A5,
  input  A4,
  input  A0,
  input  A2,
  input  A1,
  input  A6,
  input  A3,
  input  A7,
  output Cout,
  output S0,
  output S1,
  output S2,
  output S3,
  output S5,
  output S6,
  output S7,
  output S4
);

  wire ic_74283_1_p2, ic_74283_1_p12, ic_74283_1_p14, ic_74283_2_p11, ic_74283_2_p13, xor_1_out, xor_2_out,
       xor_5_out, xor_6_out;

  xor xor_1 (xor_1_out, Cin, B7);
  xor xor_2 (xor_2_out, Cin, B6);
  // IC_74283 ic_74283_1: pin names not known; wires that end beside it: Cin, ic_74283_1_p2, Cout, A7, A6, A5, A4, xor_1_out, S7, xor_2_out, S6, ic_74283_1_p12, S5, ic_74283_1_p14, S4
  xor xor_3 (ic_74283_1_p12, Cin, B5);
  xor xor_4 (ic_74283_1_p14, Cin, B4);
  xor xor_5 (xor_5_out, Cin, B3);
  xor xor_6 (xor_6_out, Cin, B2);
  // IC_74283 ic_74283_2: pin names not known; wires that end beside it: Cin, ic_74283_1_p2, A3, A2, A1, A0, xor_5_out, S3, xor_6_out, S2, ic_74283_2_p11, S1, ic_74283_2_p13, S0
  xor xor_7 (ic_74283_2_p11, Cin, B1);
  xor xor_8 (ic_74283_2_p13, Cin, B0);

  // Notes on the sheet:
  //   subtraction
endmodule

module _2_1__12bit__multiplexers (
  input  B11,
  input  B10,
  input  B9,
  input  B8,
  input  B7,
  input  B6,
  input  B5,
  input  B4,
  input  B3,
  input  B2,
  input  B1,
  input  B0,
  input  A8,
  input  A7,
  input  A6,
  input  A11,
  input  A5,
  input  A4,
  input  A1,
  input  A10,
  input  A9,
  input  A3,
  input  A2,
  input  A0,
  input  condition,
  output S11,
  output S10,
  output S9,
  output S4,
  output S2,
  output S0,
  output S8,
  output S3,
  output S1,
  output S5,
  output S7,
  output S6
);

  Multiplexer multiplexer_1 (.in0(A11), .in1(B11), .out(S11), .sel(condition));  // open: en
  Multiplexer multiplexer_2 (.in0(A10), .in1(B10), .out(S10), .sel(condition));  // open: en
  Multiplexer multiplexer_3 (.in0(A9), .in1(B9), .out(S9), .sel(condition));  // open: en
  Multiplexer multiplexer_4 (.in0(A8), .in1(B8), .out(S8), .sel(condition));  // open: en
  Multiplexer multiplexer_5 (.in0(A7), .in1(B7), .out(S7), .sel(condition));  // open: en
  Multiplexer multiplexer_6 (.in0(A6), .in1(B6), .out(S6), .sel(condition));  // open: en
  Multiplexer multiplexer_7 (.in0(A5), .in1(B5), .out(S5), .sel(condition));  // open: en
  Multiplexer multiplexer_8 (.in0(A4), .in1(B4), .out(S4), .sel(condition));  // open: en
  Multiplexer multiplexer_9 (.in0(A3), .in1(B3), .out(S3), .sel(condition));  // open: en
  Multiplexer multiplexer_10 (.in0(A2), .in1(B2), .out(S2), .sel(condition));  // open: en
  Multiplexer multiplexer_11 (.in0(A1), .in1(B1), .out(S1), .sel(condition));  // open: en
  Multiplexer multiplexer_12 (.in0(A0), .in1(B0), .out(S0), .sel(condition));  // open: en
endmodule

module _10_x_3_binary_multiplier (
  input  A9,
  input  A8,
  input  A7,
  input  A6,
  input  A5,
  input  A4,
  input  A3,
  input  A2,
  input  A1,
  input  A0,
  input  B2,
  input  B1,
  input  B0,
  output S11,
  output S10,
  output S9,
  output S8,
  output S7,
  output S6,
  output S5,
  output S4,
  output S3,
  output S1,
  output S0,
  output S2
);

  wire and_2_out, and_3_out, and_4_out, and_5_out, and_6_out, and_7_out, and_8_out, and_9_out, and_10_out,
       and_11_out, and_12_out, and_13_out, and_14_out, and_15_out, and_16_out, and_17_out, and_18_out,
       and_19_out, and_20_out, and_21_out, and_22_out, and_23_out, and_24_out, and_25_out, and_26_out,
       and_27_out, and_28_out, and_29_out, and_30_out, and_31_out, and_32_out, and_33_out, and_34_out,
       and_35_out, and_36_out, and_37_out, and_38_out, and_39_out;

  and and_1 (S0, B0, A0);
  and and_2 (and_2_out, A1, B0);
  and and_3 (and_3_out, A0, B1);
  and and_4 (and_4_out, A2, B0);
  and and_5 (and_5_out, A1, B1);
  and and_6 (and_6_out, A0, B2);
  and and_7 (and_7_out, A3, B0);
  and and_8 (and_8_out, A2, B1);
  and and_9 (and_9_out, A1, B2);
  and and_10 (and_10_out, A4, B0);
  and and_11 (and_11_out, A3, B1);
  and and_12 (and_12_out, A2, B2);
  and and_13 (and_13_out, A5, B0);
  and and_14 (and_14_out, A4, B1);
  and and_15 (and_15_out, A3, B2);
  and and_16 (and_16_out, A6, B0);
  and and_17 (and_17_out, A5, B1);
  and and_18 (and_18_out, A4, B2);
  and and_19 (and_19_out, A7, B0);
  and and_20 (and_20_out, A6, B1);
  and and_21 (and_21_out, A5, B2);
  and and_22 (and_22_out, A8, B0);
  and and_23 (and_23_out, A7, B1);
  and and_24 (and_24_out, A6, B2);
  and and_25 (and_25_out, A9, B0);
  and and_26 (and_26_out, A8, B1);
  and and_27 (and_27_out, A7, B2);
  and and_28 (and_28_out, A9, B1);
  and and_29 (and_29_out, A8, B2);
  xor xor_1 (S1, and_2_out, and_3_out);
  and and_30 (and_30_out, and_2_out, and_3_out);
  ExactlyOne xor_2 (.out(S2), .in0(and_30_out), .in1(and_4_out), .in2(and_5_out), .in3(and_6_out));
  and and_31 (and_31_out, and_4_out, and_5_out, and_6_out);
  ExactlyOne xor_3 (.out(S3), .in0(and_31_out), .in1(and_7_out), .in2(and_8_out), .in3(and_9_out));
  and and_32 (and_32_out, and_7_out, and_8_out, and_9_out);
  ExactlyOne xor_4 (.out(S4), .in0(and_32_out), .in1(and_10_out), .in2(and_11_out), .in3(and_12_out));
  and and_33 (and_33_out, and_10_out, and_11_out, and_12_out);
  ExactlyOne xor_5 (.out(S5), .in0(and_33_out), .in1(and_13_out), .in2(and_14_out), .in3(and_15_out));
  and and_34 (and_34_out, and_13_out, and_14_out, and_15_out);
  ExactlyOne xor_6 (.out(S6), .in0(and_34_out), .in1(and_16_out), .in2(and_17_out), .in3(and_18_out));
  and and_35 (and_35_out, and_16_out, and_17_out, and_18_out);
  and and_36 (and_36_out, and_19_out, and_20_out, and_21_out);
  and and_37 (and_37_out, and_22_out, and_23_out, and_24_out);
  ExactlyOne xor_7 (.out(S7), .in0(and_35_out), .in1(and_19_out), .in2(and_20_out), .in3(and_21_out));
  ExactlyOne xor_8 (.out(S8), .in0(and_36_out), .in1(and_22_out), .in2(and_23_out), .in3(and_24_out));
  ExactlyOne xor_9 (.out(S9), .in0(and_37_out), .in1(and_25_out), .in2(and_26_out), .in3(and_27_out));
  and and_38 (and_38_out, and_25_out, and_26_out, and_27_out);
  ExactlyOne xor_10 (.out(S10), .in0(and_38_out), .in1(and_28_out), .in2(and_29_out));
  and and_39 (and_39_out, and_28_out, and_29_out);
  and and_40 (S11, and_39_out, A9, B2);

  // Notes on the sheet:
  //   P0
  //   P1
  //   p2
  //   p3
  //   p4
  //   p5
  //   p6
  //   p7
  //   p8
  //   p11
  //   p9
  //   p10
endmodule

module _8X3_multiplier (
  input  B2,
  input  B1,
  input  B0,
  input  A1,
  input  A5,
  input  A3,
  input  A7,
  input  A2,
  input  A0,
  input  A6,
  input  A4,
  output S9,
  output S8,
  output S7,
  output S6,
  output S5,
  output S4,
  output S2,
  output S1,
  output S0,
  output S3
);

  wire and_1_out, and_3_out, and_4_out, and_5_out, and_6_out, and_7_out, and_8_out, and_9_out, ic_74283_1_p1,
       ic_74283_1_p3, ic_74283_1_p8, ic_74283_1_p10, ic_74283_1_p11, ic_74283_1_p12, ic_74283_1_p13,
       ic_74283_1_p14, ic_74283_1_p15, ic_74283_2_p2, ic_74283_2_p7, ic_74283_2_p9, ic_74283_2_p11,
       ic_74283_3_p2, ic_74283_3_p8, ic_74283_3_p9, ic_74283_3_p10, ic_74283_3_p11, ic_74283_3_p12,
       ic_74283_3_p13, ic_74283_3_p14, ic_74283_4_p2, ic_74283_4_p7, ic_74283_4_p9, ic_74283_4_p11,
       ic_74283_4_p13;

  and and_1 (and_1_out, B1, A7);
  and and_2 (S9, B2, A7, ic_74283_4_p2);
  and and_3 (and_3_out, B1, A3);
  and and_4 (and_4_out, B1, A6);
  and and_5 (and_5_out, B1, A2);
  and and_6 (and_6_out, B1, A1);
  and and_7 (and_7_out, B1, A5);
  and and_8 (and_8_out, B1, A0);
  // IC_74283 ic_74283_1: pin names not known; wires that end beside it: ic_74283_1_p1, 1'b0, ic_74283_1_p3, and_3_out, and_5_out, and_6_out, and_8_out, ic_74283_1_p8, ic_74283_1_p1, ic_74283_1_p10, ic_74283_1_p11, ic_74283_1_p12, ic_74283_1_p13, ic_74283_1_p14, ic_74283_1_p15
  // IC_74283 ic_74283_2: pin names not known; wires that end beside it: ic_74283_1_p3, ic_74283_2_p2, ic_74283_1_p1, ic_74283_1_p11, ic_74283_1_p13, ic_74283_1_p15, ic_74283_2_p7, S4, ic_74283_2_p9, S3, ic_74283_2_p11, S2, 1'b0, S1
  and and_9 (and_9_out, B1, A4);
  // IC_74283 ic_74283_3: pin names not known; wires that end beside it: ic_74283_2_p2, ic_74283_3_p2, and_1_out, and_4_out, and_7_out, and_9_out, 1'b0, ic_74283_3_p8, ic_74283_3_p9, ic_74283_3_p10, ic_74283_3_p11, ic_74283_3_p12, ic_74283_3_p13, ic_74283_3_p14
  // IC_74283 ic_74283_4: pin names not known; wires that end beside it: ic_74283_3_p2, ic_74283_4_p2, ic_74283_3_p8, ic_74283_3_p10, ic_74283_3_p12, ic_74283_3_p14, ic_74283_4_p7, S8, ic_74283_4_p9, S7, ic_74283_4_p11, S6, ic_74283_4_p13, S5
  and and_10 (ic_74283_1_p8, B0, A4);
  and and_11 (ic_74283_2_p7, B2, A2);
  and and_12 (ic_74283_4_p7, B2, A6);
  and and_13 (ic_74283_1_p10, B0, A3);
  and and_14 (ic_74283_2_p9, B2, A1);
  and and_15 (ic_74283_3_p9, B0, A7);
  and and_16 (ic_74283_4_p9, B2, A5);
  and and_17 (ic_74283_1_p12, B0, A2);
  and and_18 (ic_74283_2_p11, B2, A0);
  and and_19 (ic_74283_3_p13, B0, A5);
  and and_20 (ic_74283_3_p11, B0, A6);
  and and_21 (ic_74283_4_p11, B2, A4);
  and and_22 (ic_74283_4_p13, B2, A3);
  and and_23 (ic_74283_1_p14, B0, A1);
  and and_24 (S0, B0, A0);
endmodule
