// Logisim project kashi project EL.circ as structural Verilog: 1 circuit, main circuit main
module main (
  input  in_1,
  input  in_2,
  input  in_3,
  input  in_4,
  input  in_5,
  input  in_6,
  input  in_7,
  input  in_8,
  input  subtraction,
  input  in_10,
  input  in_11,
  input  in_12,
  input  in_13,
  input  in_14,
  input  in_15,
  input  in_16,
  input  in_17,
  input  in_18,
  input  in_19,
  input  in_20,
  input  in_21,
  input  in_22,
  input  in_23,
  input  in_24,
  input  initial_charges,
  input  in_26,
  input  in_27,
  input  in_28,
  input  in_29,
  input  in_30,
  input  in_31,
  input  in_32,
  input  in_33
);

  wire and_1_out, and_3_out, and_4_out, and_5_out, and_6_out, and_7_out, and_8_out, and_9_out, ic_74283_1_p2,
       ic_74283_1_p3, ic_74283_1_p5, ic_74283_1_p6, ic_74283_1_p7, ic_74283_1_p8, ic_74283_1_p9,
       ic_74283_2_p2, ic_74283_2_p3, ic_74283_2_p9, ic_74283_2_p11, ic_74283_2_p13, ic_74283_2_p14,
       ic_74283_2_p15, ic_74283_3_p1, ic_74283_3_p3, ic_74283_3_p8, ic_74283_3_p10, ic_74283_3_p11,
       ic_74283_3_p12, ic_74283_3_p13, ic_74283_3_p14, ic_74283_3_p15, ic_74283_4_p2, ic_74283_4_p7,
       ic_74283_4_p8, ic_74283_4_p9, ic_74283_4_p10, ic_74283_4_p11, ic_74283_4_p12, ic_74283_4_p14,
       ic_74283_5_p2, ic_74283_5_p8, ic_74283_5_p9, ic_74283_5_p10, ic_74283_5_p11, ic_74283_5_p12,
       ic_74283_5_p13, ic_74283_5_p14, ic_74283_6_p2, ic_74283_6_p7, ic_74283_6_p9, ic_74283_6_p10,
       ic_74283_6_p11, ic_74283_6_p12, ic_74283_6_p13, ic_74283_6_p14, ic_74283_7_p1, ic_74283_7_p4,
       ic_74283_7_p6, ic_74283_7_p8, ic_74283_7_p10, ic_74283_8_p8, ic_74283_8_p10, ic_74283_8_p11,
       ic_74283_8_p12, ic_74283_8_p13, ic_74283_8_p14, ic_74283_9_p4, ic_74283_9_p6, ic_74283_9_p8,
       ic_74283_9_p9, ic_74283_9_p10, multiplexer_1_out, multiplexer_2_out, multiplexer_3_out,
       multiplexer_4_out, multiplexer_5_out, multiplexer_6_out, multiplexer_7_out, multiplexer_8_out,
       multiplexer_9_out, multiplexer_10_out, multiplexer_11_out, multiplexer_12_out, xor_1_out, xor_2_out,
       xor_3_out, xor_5_out, xor_6_out;

  Multiplexer multiplexer_1 (
    .in0(in_24), .in1(ic_74283_1_p3), .out(multiplexer_1_out), .sel(ic_74283_2_p3));  // open: en
  // IC_74283 ic_74283_1: pin names not known; wires that end beside it: in_20, ic_74283_1_p2, ic_74283_1_p3, in_24, ic_74283_1_p5, ic_74283_1_p6, ic_74283_1_p7, ic_74283_1_p8, ic_74283_1_p9
  Multiplexer multiplexer_2 (
    .in0(in_24), .in1(ic_74283_1_p5), .out(multiplexer_2_out), .sel(ic_74283_2_p3));  // open: en
  and and_1 (and_1_out, in_19, ic_74283_2_p9);
  and and_2 (ic_74283_1_p6, in_18, ic_74283_2_p9, ic_74283_6_p2);
  Multiplexer multiplexer_3 (
    .in0(in_24), .in1(ic_74283_1_p7), .out(multiplexer_3_out), .sel(ic_74283_2_p3));  // open: en
  xor xor_1 (xor_1_out, subtraction, in_5);
  xor xor_2 (xor_2_out, subtraction, in_6);
  and and_3 (and_3_out, in_19, ic_74283_8_p10);
  and and_4 (and_4_out, in_19, ic_74283_8_p8);
  and and_5 (and_5_out, in_19, ic_74283_2_p11);
  xor xor_3 (xor_3_out, subtraction, in_7);
  // IC_74283 ic_74283_2: pin names not known; wires that end beside it: subtraction, ic_74283_2_p2, ic_74283_2_p3, in_15, in_16, in_17, in_11, xor_1_out, ic_74283_2_p9, xor_2_out, ic_74283_2_p11, xor_3_out, ic_74283_2_p13, ic_74283_2_p14, ic_74283_2_p15
  and and_6 (and_6_out, in_19, ic_74283_8_p12);
  and and_7 (and_7_out, in_19, ic_74283_2_p13);
  Multiplexer multiplexer_4 (
    .in0(in_24), .in1(ic_74283_1_p9), .out(multiplexer_4_out), .sel(ic_74283_2_p3));  // open: en
  and and_8 (and_8_out, in_19, ic_74283_8_p14);
  // IC_74283 ic_74283_3: pin names not known; wires that end beside it: ic_74283_3_p1, in_21, ic_74283_3_p3, and_4_out, and_3_out, and_6_out, and_8_out, ic_74283_3_p8, ic_74283_3_p1, ic_74283_3_p10, ic_74283_3_p11, ic_74283_3_p12, ic_74283_3_p13, ic_74283_3_p14, ic_74283_3_p15, in_19
  // IC_74283 ic_74283_4: pin names not known; wires that end beside it: ic_74283_3_p3, ic_74283_4_p2, ic_74283_3_p1, ic_74283_3_p11, ic_74283_3_p13, ic_74283_3_p15, ic_74283_4_p7, ic_74283_4_p8, ic_74283_4_p9, ic_74283_4_p10, ic_74283_4_p11, ic_74283_4_p12, in_22, ic_74283_4_p14, in_19
  and and_9 (and_9_out, in_19, ic_74283_2_p15);
  // IC_74283 ic_74283_5: pin names not known; wires that end beside it: ic_74283_4_p2, ic_74283_5_p2, and_1_out, and_5_out, and_7_out, and_9_out, in_23, ic_74283_5_p8, ic_74283_5_p9, ic_74283_5_p10, ic_74283_5_p11, ic_74283_5_p12, ic_74283_5_p13, ic_74283_5_p14
  // IC_74283 ic_74283_6: pin names not known; wires that end beside it: ic_74283_5_p2, ic_74283_6_p2, ic_74283_5_p8, ic_74283_5_p10, ic_74283_5_p12, ic_74283_5_p14, ic_74283_6_p7, ic_74283_1_p8, ic_74283_6_p9, ic_74283_6_p10, ic_74283_6_p11, ic_74283_6_p12, ic_74283_6_p13, ic_74283_6_p14
  Multiplexer multiplexer_5 (
    .in0(in_29), .in1(ic_74283_7_p4), .out(multiplexer_5_out), .sel(ic_74283_2_p3));  // open: en
  xor xor_4 (ic_74283_2_p14, subtraction, in_8);
  and and_10 (ic_74283_3_p8, in_20, ic_74283_2_p15);
  and and_11 (ic_74283_4_p7, in_18, ic_74283_8_p10);
  and and_12 (ic_74283_6_p7, in_18, ic_74283_2_p11);
  // IC_74283 ic_74283_7: pin names not known; wires that end beside it: ic_74283_7_p1, ic_74283_1_p2, ic_74283_6_p10, ic_74283_7_p4, ic_74283_6_p12, ic_74283_7_p6, ic_74283_6_p14, ic_74283_7_p8, ic_74283_4_p8, ic_74283_7_p10
  Multiplexer multiplexer_6 (
    .in0(in_30), .in1(ic_74283_7_p6), .out(multiplexer_6_out), .sel(ic_74283_2_p3));  // open: en
  and and_13 (ic_74283_3_p10, in_20, ic_74283_8_p8);
  and and_14 (ic_74283_4_p9, in_18, ic_74283_8_p12);
  and and_15 (ic_74283_5_p9, in_20, ic_74283_2_p9);
  and and_16 (ic_74283_6_p9, in_18, ic_74283_2_p13);
  Multiplexer multiplexer_7 (
    .in0(in_31), .in1(ic_74283_7_p8), .out(multiplexer_7_out), .sel(ic_74283_2_p3));  // open: en
  xor xor_5 (xor_5_out, subtraction, in_1);
  and and_17 (ic_74283_3_p12, in_20, ic_74283_8_p10);
  and and_18 (ic_74283_4_p11, in_18, ic_74283_8_p14);
  and and_19 (ic_74283_5_p13, in_20, ic_74283_2_p13);
  and and_20 (ic_74283_5_p11, in_20, ic_74283_2_p11);
  and and_21 (ic_74283_6_p13, in_18, ic_74283_8_p8);
  and and_22 (ic_74283_6_p11, in_18, ic_74283_2_p15);
  xor xor_6 (xor_6_out, subtraction, in_2);
  // IC_74283 ic_74283_8: pin names not known; wires that end beside it: subtraction, ic_74283_2_p2, in_12, in_13, in_14, in_10, xor_5_out, ic_74283_8_p8, xor_6_out, ic_74283_8_p10, ic_74283_8_p11, ic_74283_8_p12, ic_74283_8_p13, ic_74283_8_p14
  and and_23 (ic_74283_3_p14, in_20, ic_74283_8_p12);
  Multiplexer multiplexer_8 (
    .in0(in_32), .in1(ic_74283_7_p10), .out(multiplexer_8_out), .sel(ic_74283_2_p3));  // open: en
  xor xor_7 (ic_74283_8_p11, subtraction, in_3);
  Multiplexer multiplexer_9 (
    .in0(initial_charges), .in1(ic_74283_9_p4), .out(multiplexer_9_out), .sel(ic_74283_2_p3));  // open: en
  xor xor_8 (ic_74283_8_p13, subtraction, in_4);
  // IC_74283 ic_74283_9: pin names not known; wires that end beside it: in_33, ic_74283_7_p1, ic_74283_4_p10, ic_74283_9_p4, ic_74283_4_p12, ic_74283_9_p6, ic_74283_4_p14, ic_74283_9_p8, ic_74283_9_p9, ic_74283_9_p10
  Multiplexer multiplexer_10 (
    .in0(in_26), .in1(ic_74283_9_p6), .out(multiplexer_10_out), .sel(ic_74283_2_p3));  // open: en
  and and_24 (ic_74283_9_p9, in_20, ic_74283_8_p14);
  Multiplexer multiplexer_11 (
    .in0(in_27), .in1(ic_74283_9_p8), .out(multiplexer_11_out), .sel(ic_74283_2_p3));  // open: en
  Multiplexer multiplexer_12 (
    .in0(in_28), .in1(ic_74283_9_p10), .out(multiplexer_12_out), .sel(ic_74283_2_p3));  // open: en

  // Notes on the sheet:
  //   per km fare
  //   mandatory distance
  //   distance of travel
endmodule
